# Fritzing sketch VChiller circuit plan (saved by Fritzing 0.9.3b)
breadboards: 1

parts:
  Part1 = Arduino Mega ADK (Rev3)
  DS1 = DS18B20 1-Wire Temperature Sensor [part_number=DS18B20]
  DS2 = DS18B20 1-Wire Temperature Sensor [part_number=DS18B20]
  Motor_Shield = IC, SIP package, 7 pins
  DC_Fan = DC Motor
  R1 = Resistor [tolerance=±5% resistance=4.7k package="2512 [SMD]"]
  R2 = Resistor [tolerance=±5% resistance=4.7k package="2512 [SMD]"]
  R3 = Rotary Potentiometer (Small) [maximum_resistance=10kΩ package=THT]
  Pressure_sensor = MPX4250AP pressure sensor [part_number=MPX]
  DC_Water_Pump = DC Motor
  Relay_module = QFN-24 [chip_label="8 relays" package=QFN]
  AC_Power_plug = Power plug
  AC_Vacuum_Pump = DC Motor
  AC_Solenoid_Valve = DC Motor
  AC_Fans1 = DC Motor
  AC_Fans2 = DC Motor

nets:
  N1: Part1.A0, R3.wiper
  N2: Part1.A1, Pressure_sensor.V_out
  N3: Part1.D14/TX3, DS1.DQ, R2.Pin_1
  GND: Part1.GND, DS2.GND, Motor_Shield.pin2, R3.leg1, Pressure_sensor.GND, DC_Water_Pump.pin_2
  N4: Part1.D13_PWM, Relay_module.1
  N5: Part1.D12_PWM, Relay_module.2
  N6: Part1.D11_PWM, Relay_module.3
  N7: Part1.D10_PWM, Relay_module.4
  N8: Part1.D9_PWM, Relay_module.5
  N9: Part1.D8_PWM, Relay_module.6
  12V: Part1.VIN, Motor_Shield.pin1, Relay_module.9
  N10: Part1.D2_PWM, DS2.DQ, R1.Pin_1
  N11: Part1.D3_PWM, Motor_Shield.pin5
  N12: Part1.D4_PWM, Motor_Shield.pin4
  N13: Part1.D5_PWM, Motor_Shield.pin3
  N14: Part1.D6_PWM, Relay_module.8
  N15: Part1.D7_PWM, Relay_module.7
  N16: DS1.GND, Relay_module.12
  5V: DS1.VDD, DS2.VDD, R1.Pin_0, R2.Pin_0, R3.leg2, Pressure_sensor.Vs, Relay_module.11
  N17: Motor_Shield.pin6, DC_Fan.pin_1
  N18: Motor_Shield.pin7, DC_Fan.pin_2
  N19: DC_Water_Pump.pin_1, Relay_module.23
  N20: Relay_module.19, AC_Fans2.pin_1
  N21: Relay_module.20, AC_Fans1.pin_1
  N22: Relay_module.21, AC_Solenoid_Valve.pin_1
  N23: Relay_module.22, AC_Vacuum_Pump.pin_1
  N24: Relay_module.24, AC_Power_plug.VCC
  N25: AC_Power_plug.GND, AC_Vacuum_Pump.pin_2, AC_Solenoid_Valve.pin_2, AC_Fans1.pin_2, AC_Fans2.pin_2
